// Logisim project Aula1309.circ as structural Verilog: 1 circuit, main circuit main
module main (
  input  in_1,
  input  in_2,
  input  in_3,
  input  in_4,
  input  in_5,
  input  in_6,
  input  in_7,
  input  in_8,
  input  in_9,
  input  in_10,
  input  in_11,
  input  in_12,
  input  in_13,
  input  in_14,
  input  in_15,
  input  in_16,
  input  in_17,
  input  in_18,
  input  in_19,
  input  in_20,
  input  in_21,
  output out_22,
  output out_23,
  output out_24,
  output out_25,
  output out_26,
  output out_27,
  output out_28
);

  wire and_1_out, and_2_out, and_3_out, and_4_out, and_5_out, and_6_out, and_7_out, and_8_out, and_9_out,
       and_10_out, and_11_out, and_12_out, and_13_out, and_14_out, and_15_out, and_16_out, and_17_out,
       nand_1_out, nand_2_out, not_1_out, not_2_out, not_3_out, not_4_out, not_5_out, not_6_out, not_7_out,
       not_8_out, not_9_out, not_10_out, not_11_out, not_12_out, not_13_out, not_14_out, or_3_out;

  not not_1 (not_1_out, in_2);
  not not_2 (not_2_out, in_7);
  not not_3 (not_3_out, in_10);
  not not_4 (not_4_out, in_16);
  not not_5 (not_5_out, in_18);
  not not_6 (not_6_out, in_21);
  and and_1 (and_1_out, not_1_out, not_2_out, not_3_out);
  and and_2 (and_2_out, in_2, not_2_out, not_3_out);
  and and_3 (and_3_out, in_2, in_7, in_10);
  not not_7 (not_7_out, in_14);
  or or_1 (out_24, and_1_out, and_2_out, and_3_out);
  and and_4 (and_4_out, not_7_out, not_4_out, not_5_out, not_6_out);
  and and_5 (and_5_out, not_7_out, in_16, in_18, in_21);
  and and_6 (and_6_out, in_14, not_4_out, in_18, not_6_out);
  and and_7 (and_7_out, in_14, in_16, in_18, not_6_out);
  or or_2 (out_27, and_4_out, and_5_out, and_6_out, and_7_out);
  and and_8 (and_8_out, in_1, in_4);
  nand nand_1 (nand_1_out, in_6, in_8);
  not not_8 (not_8_out, in_9);
  xnor xnor_1 (out_22, and_8_out, nand_1_out);
  nand nand_2 (nand_2_out, not_8_out, in_11);
  or or_3 (or_3_out, in_11, in_12);
  not not_9 (not_9_out, in_19);
  not not_10 (not_10_out, in_20);
  or or_4 (out_25, nand_2_out, or_3_out);
  not not_11 (not_11_out, in_13);
  not not_12 (not_12_out, in_15);
  and and_9 (and_9_out, not_9_out, not_10_out);
  and and_10 (and_10_out, not_10_out, in_19);
  not not_13 (not_13_out, in_3);
  not not_14 (not_14_out, in_5);
  and and_11 (and_11_out, not_11_out, not_12_out, in_17);
  and and_12 (and_12_out, not_11_out, in_15, in_17);
  and and_13 (and_13_out, in_13, not_12_out, in_17);
  and and_14 (and_14_out, in_13, in_15, in_17);
  or or_5 (out_28, and_9_out, and_10_out);
  and and_15 (and_15_out, not_13_out, not_14_out);
  and and_16 (and_16_out, not_13_out, in_5);
  and and_17 (and_17_out, in_3, in_5);
  or or_6 (out_23, and_15_out, and_16_out, and_17_out);
  or or_7 (out_26, and_11_out, and_12_out, and_13_out, and_14_out);
endmodule
