// Logisim project circuito.circ as structural Verilog: 3 circuits, main circuit main
module main (
  input  in_1,
  input  in_2,
  input  in_3,
  input  [1:0] in_4,
  input  in_5,
  input  in_6,
  input  [1:0] in_7,
  input  in_8,
  input  in_9,
  input  in_10,
  input  in_11,
  input  in_12,
  input  in_13,
  input  in_14,
  input  in_15,
  input  [2:0] in_16,
  input  [2:0] in_17,
  input  [1:0] in_18,
  input  [1:0] in_19,
  output [2:0] out_20,
  output out_21,
  output out_22,
  output out_23,
  output out_24,
  output out_25,
  output out_26,
  output out_27,
  output [3:0] out_28,
  output [2:0] out_29
);

  wire adder_2_cout, meio_somador_1_out_4, meio_somador_2_out_4, somado_completo_2_out_5;

  not not_1 (out_21, in_1);
  and and_1 (out_22, in_2, in_5);
  or or_1 (out_24, in_8, in_10);
  xor xor_1 (out_26, in_12, in_14);
  Adder #(.width(1)) adder_1 (.a(in_18[1]), .b(in_19[1]), .out(out_29[1]), .cin(adder_2_cout), .cout(out_29[2]));
  Adder #(.width(1)) adder_2 (.a(in_18[0]), .b(in_19[1]), .out(out_29[0]), .cout(adder_2_cout));  // open: cin
  nand nand_1 (out_23, in_3, in_6);
  nor nor_1 (out_25, in_9, in_11);
  xnor xnor_1 (out_27, in_13, in_15);
  meio_somador meio_somador_1 (.in_1(in_4[0]), .in_2(in_7[0]), .out_3(out_20[0]), .out_4(meio_somador_1_out_4));
  meio_somador meio_somador_2 (.in_1(in_16[0]), .in_2(in_17[0]), .out_3(out_28[0]), .out_4(meio_somador_2_out_4));
  Somado_completo somado_completo_1 (
    .in_1(meio_somador_1_out_4), .in_2(in_4[1]), .in_3(in_7[1]), .out_4(out_20[1]), .out_5(out_20[2]));
  Somado_completo somado_completo_2 (
    .in_1(in_16[1]), .in_2(in_17[1]), .in_3(meio_somador_2_out_4), .out_4(out_28[1]),
    .out_5(somado_completo_2_out_5));
  Somado_completo somado_completo_3 (
    .in_1(in_16[2]), .in_2(somado_completo_2_out_5), .in_3(in_17[2]), .out_4(out_28[2]), .out_5(out_28[3]));

  assign in_19[0] = in_19[1];

  // Notes on the sheet:
  //   NOT
  //   AND
  //   OR
  //   XOR
  //   NAND
  //   NOR
  //   XNOR
endmodule

module meio_somador (
  input  in_1,
  input  in_2,
  output out_3,
  output out_4
);

  xor xor_1 (out_3, in_1, in_2);
  and and_1 (out_4, in_1, in_2);
endmodule

module Somado_completo (
  input  in_1,
  input  in_2,
  input  in_3,
  output out_4,
  output out_5
);

  wire and_1_out, and_2_out, and_3_out, xor_1_out;

  xor xor_1 (xor_1_out, in_1, in_2);
  and and_1 (and_1_out, in_2, in_1);
  and and_2 (and_2_out, in_2, in_3);
  and and_3 (and_3_out, in_1, in_3);
  xor xor_2 (out_4, xor_1_out, in_3);
  or or_1 (out_5, and_1_out, and_2_out, and_3_out);
endmodule
